// Logisim project bin2bcdConverter.circ as structural Verilog: 2 circuits, main circuit converter
module converter (
  input  [6:0] bin,
  output [3:0] lowBcd,
  output [3:0] highBcd
);

  wire comparator_1_eq, not_1_out;
  wire [7:0] rom_1_data;

  ROM #(.addrWidth(7)) rom_1 (.addr(bin), .data(rom_1_data), .sel(1'b1));
  Comparator #(.width(4)) comparator_1 (.a(rom_1_data[3:0]), .b(4'b1010), .eq(comparator_1_eq));  // open: gt, lt
  not not_1 (not_1_out, comparator_1_eq);
  assign lowBcd = not_1_out ? rom_1_data[3:0] : 4'bz;  // Controlled_Buffer controlled_buffer_1
  assign highBcd = not_1_out ? rom_1_data[7:4] : 4'bz;  // Controlled_Buffer controlled_buffer_2

  // Notes on the sheet:
  //   binary to bcd converter (range 0 .. 99dec incl.)
  //   contents of rom_1 (hex, n*v repeats v):
  //   0 1 2 3 4 5 6 7 8 9 10 11 12 13 14 15 16 17 18 19 20 21 22 23 24 25 26 27 28 29 30 31 32 33 34 35 36
  //   37 38 39 40 41 42 43 44 45 46 47 48 49 50 51 52 53 54 55 56 57 58 59 60 61 62 63 64 65 66 67 68 69
  //   70 71 72 73 74 75 76 77 78 79 80 81 82 83 84 85 86 87 88 89 90 91 92 93 94 95 96 97 98 99 28*a
endmodule

module test (
  input  [6:0] bin
);

  wire [3:0] converter_1_highbcd, converter_1_lowbcd;

  converter converter_1 (.bin(bin), .lowBcd(converter_1_lowbcd), .highBcd(converter_1_highbcd));
  Hex_Digit_Display hex_digit_display_1 (.value(converter_1_lowbcd));  // open: dp
  Hex_Digit_Display hex_digit_display_2 (.value(converter_1_highbcd));  // open: dp

  // Notes on the sheet:
  //   test configuration for binary to bcd converter (range 0 .. 99dec incl.)
endmodule
