// Logisim project fiboGenerator_V0.circ as structural Verilog
module main (
  input  [3:0] In0,
  input  [3:0] In1,
  input  Start_nStop
);

  wire CP_out, data_path_1_feedback, Reset_out;
  wire [3:0] converter_1_highbcd, converter_1_lowbcd;
  wire [4:0] controller_1_state;
  wire [6:0] data_path_1_dout;
  wire [7:0] controller_1_din;
  wire [10:0] controller_1_control_word;

  Button Reset (.out(Reset_out));
  Clock CP (.out(CP_out));
  data_path data_path_1 (
    .din(controller_1_din), .control_word(controller_1_control_word), .clk(CP_out), .dout(data_path_1_dout),
    .feedback(data_path_1_feedback), .reset(Reset_out), .In0(In0), .In1(In1), .start(Start_nStop));
  controller controller_1 (
    .state(controller_1_state), .control_word(controller_1_control_word), .feedback(data_path_1_feedback),
    .din(controller_1_din), .clk(CP_out), .reset(Reset_out), .start(Start_nStop));
  // Probe on data_path_1_feedback
  // Probe on controller_1_state
  converter converter_1 (.bin(data_path_1_dout), .lowBcd(converter_1_lowbcd), .highBcd(converter_1_highbcd));
  Hex_Digit_Display hex_digit_display_1 (.value(converter_1_lowbcd));  // open: dp
  Hex_Digit_Display hex_digit_display_2 (.value(converter_1_highbcd));  // open: dp

  // Notes on the sheet:
  //   state
endmodule

module controller (
  input  feedback,
  input  start,
  input  clk,
  input  reset,
  output [7:0] din,
  output [4:0] state,
  output [10:0] control_word
);

  wire and_1_out;
  wire [4:0] rom_1_data;

  and and_1 (and_1_out, start, clk);
  ROM #(.addrWidth(6), .dataWidth(5)) rom_1 (.addr({feedback, state}), .data(rom_1_data));  // open: sel
  Register #(.width(5)) register_1 (.D(rom_1_data), .Q(state), .clk(and_1_out), .clr(reset));  // open: en
  ROM #(.addrWidth(5)) rom_2 (.addr(state), .data(din));  // open: sel
  ROM #(.addrWidth(5), .dataWidth(11)) rom_3 (.addr(state), .data(control_word));  // open: sel

  // Notes on the sheet:
  //   Next-State-Logic
  //   Output-Logic for
  //   Data In Value
  //   Output-Logic for
  //   Control Word
endmodule

module data_path (
  input  [3:0] In0,
  input  [3:0] In1,
  input  [7:0] din,
  input  start,
  input  clk,
  input  reset,
  input  [10:0] control_word,
  output [6:0] dout,
  output feedback
);

  wire and_1_out;
  wire [7:0] alu_1_result, bit_extender_1_out, bit_extender_2_out, multiplexer_1_out, undriven, undriven_2;

  assign bit_extender_1_out = {{4{1'b0}}, In0};  // Bit_Extender bit_extender_1
  and and_1 (and_1_out, start, clk);
  assign bit_extender_2_out = {{4{1'b0}}, In1};  // Bit_Extender bit_extender_2
  Multiplexer #(.select(2), .width(8), .enable("false")) multiplexer_1 (
    .in0(alu_1_result), .in1(bit_extender_1_out), .in2(bit_extender_2_out), .in3(din),
    .out(multiplexer_1_out), .sel(control_word[8:7]));
  // Probe on multiplexer_1_out
  // Probe on control_word[10:9]
  // Probe on control_word[8:7]
  // Probe on control_word[6]
  // Probe on control_word[5:4]
  // Probe on control_word[3:2]
  // Probe on control_word[1:0]
  // Probe on alu_1_result
  // Probe on undriven
  // Probe on undriven_2
  regfile regfile_1 ();
  ALU alu_1 (.feedback(feedback), .op0(undriven), .result(alu_1_result), .opSel(control_word[10:9]), .op1(undriven_2));
endmodule

module ALU (
  input  [7:0] op0,
  input  [7:0] op1,
  input  [1:0] opSel,
  output [7:0] result,
  output feedback
);

  wire [7:1] multiplexer_1_out;

  Adder adder_1 (.a(op0), .b(op1), .out(result));  // open: cin, cout
  Multiplexer #(.select(5), .width(8)) multiplexer_1 (
    .in15(result), .out({multiplexer_1_out, feedback}));  // open: in0, in1, in2, in3, in4, in5, in6, in7, in8, in9, in10, in11, in12, in13, in14, in16, in17, in18, in19, in20, in21, in22, in23, in24, in25, in26, in27, in28, in29, in30, in31, sel, en
  // Pins of 1 and 8 bits meet at {multiplexer_1_out, feedback}
endmodule
